# Fritzing sketch Hbridge (saved by Fritzing 0.7.10b)
breadboards: 1

parts:
  IC1 = IC, DIP package, 14 pins [chip_label=IC]
  J1 = female pin header, 3 pins [form="♀ (female)"]
  R1 = Resistor [tolerance=±5% resistance=2k package=THT]
  R2 = Resistor [tolerance=±5% resistance=2k package=THT]
  R3 = Resistor [tolerance=±5% resistance=2k package=THT]
  J2 = female pin header, 3 pins [form="♀ (female)"]
  C1 = Ceramic Capacitor [capacitance=100nF package="100 mil [THT, multilayer]"]
  R4 = Resistor [tolerance=±5% resistance=22k package=THT]
  R5 = Resistor [tolerance=±5% resistance=22k package=THT]
  Q1 = Basic FET N-Channel [package="TO220 [THT]"]
  Q2 = Basic FET N-Channel [package="TO220 [THT]"]
  Q3 = Basic FET N-Channel [package="TO220 [THT]"]
  Q4 = Basic FET N-Channel [package="TO220 [THT]"]
  J3 = female pin header, 2 pins [form="♀ (female)"]
  R6 = Resistor [tolerance=±5% resistance=5k package=THT]
  R7 = Resistor [tolerance=±5% resistance=2k package=THT]
  R8 = Resistor [tolerance=±5% resistance=2k package=THT]
  R9 = Resistor [tolerance=±5% resistance=2k package=THT]
  R10 = Resistor [tolerance=±5% resistance=2k package=THT]
  C2 = Ceramic Capacitor [capacitance=100nF package="100 mil [THT, multilayer]"]
  C3 = Electrolytic Capacitor [capacitance=1mF voltage=10V package="200 mil [THT, electrolytic]"]

nets:
  N1: IC1.pin1, Q3.gate
  N2: IC1.pin2, IC1.pin5, C1.1, R4.Pin_0
  N3: IC1.pin3, IC1.pin12, R1.Pin_1, R2.Pin_0
  N4: IC1.pin4, J1.pin1
  N5: IC1.pin6, IC1.pin9, R2.Pin_1, R3.Pin_0
  N6: IC1.pin7, Q4.gate
  N7: IC1.pin8, Q1.gate
  N8: IC1.pin10, IC1.pin13, R5.Pin_0, C2.0
  N9: IC1.pin11, J1.pin3, R1.Pin_0, C1.0, Q1.source, Q4.source, R8.Pin_1, R10.Pin_0, C2.1, C3.-
  N10: IC1.pin14, Q2.gate
  N11: J1.pin2, Q2.drain, Q3.drain, R6.Pin_0, C3.+
  N12: R3.Pin_1, J2.pin2, R6.Pin_1, R7.Pin_1, R9.Pin_1
  N13: J2.pin1, R5.Pin_1, R7.Pin_0, R10.Pin_1
  N14: J2.pin3, R4.Pin_1, R8.Pin_0, R9.Pin_0
  N15: Q1.drain, Q2.source, J3.pin1
  N16: Q3.source, Q4.drain, J3.pin2

notes:
  Rev. B1
