# Fritzing sketch HbridgePower (saved by Fritzing 0.7.7b)
breadboards: 1

parts:
  IC1 = IC, DIP package, 8 pins [chip_label=IC]
  J1 = female pin header, 2 pins [form="♀ (female)"]
  C1 = Electrolytic Capacitor [capacitance=1µF package="100 mil [THT, electrolytic]"]
  D1 = Rectifier Diode [part_number=1N4001 package="300 mil [THT]"]
  D2 = Rectifier Diode [part_number=1N4001 package="300 mil [THT]"]
  C2 = Electrolytic Capacitor [capacitance=1µF package="100 mil [THT, electrolytic]"]
  J2 = female pin header, 2 pins [form="♀ (female)"]

nets:
  N1: IC1.pin2, C1.-
  N2: IC1.pin3, IC1.pin5, J1.pin1, C2.-, J2.pin1
  N3: IC1.pin8, J1.pin2, D1.anode
  N4: C1.+, D1.cathode, D2.anode
  N5: D2.cathode, C2.+, J2.pin2

notes:
  Voltage Doubler
  Rev. 01
